// Logisim project final.circ as structural Verilog: 7 circuits, main circuit main
module _1of1stprogs (
  input  A,
  input  B,
  input  C,
  output SUM,
  output COUT
);

  wire and_1_out, and_2_out, and_3_out, and_4_out, and_5_out, and_6_out, and_7_out;

  and and_1 (and_1_out, ~A, ~B, C);  // AND_Gate
  and and_2 (and_2_out, ~A, B, ~C);  // AND_Gate
  and and_3 (and_3_out, A, ~B, ~C);  // AND_Gate
  and and_4 (and_4_out, A, B, C);
  and and_5 (and_5_out, A, B);
  and and_6 (and_6_out, B, C);
  and and_7 (and_7_out, A, C);
  or or_1 (SUM, and_1_out, and_2_out, and_3_out, and_4_out);
  or or_2 (COUT, and_5_out, and_6_out, and_7_out);
endmodule

module MUX (
  input  A,
  input  B,
  input  C,
  output out_4
);

  wire and_1_out, and_2_out;

  and and_1 (and_1_out, A, ~C);  // AND_Gate
  and and_2 (and_2_out, B, C);
  or or_1 (out_4, and_1_out, and_2_out);
endmodule

module ALU_bit (
  input  in_1,
  input  bus_i,
  input  Bus_1___i,
  input  Bus_i__1,
  input  bus_2i,
  input  in_6,
  input  in_7,
  input  in_8,
  input  in_9,
  input  in_10,
  input  in_11,
  input  in_12,
  input  in_13,
  input  in_14,
  output CARRY_OUT,
  output BUS_3
);

  wire ADD_OUT, ADD_out_2, and_1_out, and_2_out, and_3_out, AND_4_out, mux_1_out_4, not_1_out, not_2_out,
       not_3_out, not_4_out, NOT_5_out, or_1_out, or_2_out, OR_3_out, or_4_out, SHL_out, SHR_out, SUB_out,
       TCP_out, TRA1_out, undriven;

  not not_1 (not_1_out, bus_2i);
  or or_1 (or_1_out, in_7, in_11);
  or or_2 (or_2_out, in_6, in_9);
  not not_2 (not_2_out, in_11);
  and and_1 (and_1_out, not_2_out, Bus_i__1);
  MUX mux_1 (.A(bus_2i), .B(not_1_out), .C(or_1_out), .out_4(mux_1_out_4));
  not not_3 (not_3_out, or_2_out);
  and and_2 (and_2_out, not_3_out, undriven);
  _1of1stprogs u_1of1stprogs_1 (.A(and_1_out), .B(mux_1_out_4), .C(in_1), .SUM(ADD_OUT), .COUT(CARRY_OUT));
  not not_4 (not_4_out, bus_2i);
  and and_3 (and_3_out, Bus_i__1, bus_2i);
  and ADD (ADD_out_2, in_6, ADD_OUT);
  and SUB (SUB_out, in_7, ADD_OUT);
  and TCP (TCP_out, in_11, ADD_OUT);
  and NOT_5 (NOT_5_out, in_10, not_4_out);
  and AND_4 (AND_4_out, in_8, and_3_out);
  and OR_3 (OR_3_out, in_9, or_4_out);
  or or_4 (or_4_out, Bus_i__1, bus_2i);
  and SHL (SHL_out, in_12, Bus_1___i);
  and SHR (SHR_out, in_13, bus_i);
  and TRA1 (TRA1_out, in_14, Bus_i__1);
  or or_5 (BUS_3, ADD_out_2, SUB_out, TCP_out, NOT_5_out, AND_4_out, OR_3_out, SHL_out, SHR_out, TRA1_out);

  // Other names for the same wires on the sheet: ADD = in_6; AND = in_8; BUS_I___1 = bus_i; BUS_I___1_t = Bus_1___i;
  //   BUS_I_t = Bus_i__1; C_IN = in_1; C_Out = CARRY_OUT; NOT = in_10; OR = in_9; SHL = in_12; SHR = in_13;
  //   SUB = in_7; TCP = in_11; TRA1 = in_14
endmodule

module ALU_16 (
  input  [15:0] BUS_1,
  input  [15:0] BUS_2,
  input  in_3,
  input  in_4,
  input  in_5,
  input  in_6,
  input  in_7,
  input  in_8,
  input  in_9,
  input  in_10,
  input  in_11,
  output [15:0] BUS_3,
  output out_13,
  output out_14
);

  wire BUS10_t, COUT0, COUT1, COUT2, COUT3, COUT4, COUT5, COUT6, COUT7, COUT8, COUT9, COUT10, COUT11, COUT12,
       COUT13, COUT14, or_1_out;

  ALU_bit _0 (
    .in_6(in_9), .in_7(in_4), .in_8(in_6), .in_9(in_10), .in_10(in_11), .in_11(in_3), .in_12(in_8),
    .in_13(in_5), .in_14(in_7), .bus_i(BUS_1[1]), .Bus_1___i(1'b0), .Bus_i__1(BUS_1[0]), .bus_2i(BUS_2[0]),
    .in_1(or_1_out), .CARRY_OUT(COUT0), .BUS_3(BUS_3[0]));
  ALU_bit _4 (
    .in_6(in_9), .in_7(in_4), .in_8(in_6), .in_9(in_10), .in_10(in_11), .in_11(in_3), .in_12(in_8),
    .in_13(in_5), .in_14(in_7), .bus_i(BUS_1[5]), .Bus_1___i(BUS_1[3]), .Bus_i__1(BUS_1[4]),
    .bus_2i(BUS_2[4]), .in_1(COUT3), .CARRY_OUT(COUT4), .BUS_3(BUS_3[4]));
  ALU_bit _8 (
    .in_6(in_9), .in_7(in_4), .in_8(in_6), .in_9(in_10), .in_10(in_11), .in_11(in_3), .in_12(in_8),
    .in_13(in_5), .in_14(in_7), .bus_i(BUS_1[9]), .Bus_1___i(BUS_1[7]), .Bus_i__1(BUS_1[8]),
    .bus_2i(BUS_2[8]), .in_1(COUT7), .CARRY_OUT(COUT8), .BUS_3(BUS_3[8]));
  ALU_bit _12 (
    .in_6(in_9), .in_7(in_4), .in_8(in_6), .in_9(in_10), .in_10(in_11), .in_11(in_3), .in_12(in_8),
    .in_13(in_5), .in_14(in_7), .bus_i(BUS_1[13]), .Bus_1___i(BUS_1[11]), .Bus_i__1(BUS_1[12]),
    .bus_2i(BUS_2[12]), .in_1(COUT11), .CARRY_OUT(COUT12), .BUS_3(BUS_3[12]));
  or or_1 (or_1_out, in_4, in_3);
  ALU_bit _1 (
    .in_6(in_9), .in_7(in_4), .in_8(in_6), .in_9(in_10), .in_10(in_11), .in_11(in_3), .in_12(in_8),
    .in_13(in_5), .in_14(in_7), .bus_i(BUS_1[2]), .Bus_1___i(BUS10_t), .Bus_i__1(BUS_1[1]),
    .bus_2i(BUS_2[1]), .in_1(COUT0), .CARRY_OUT(COUT1), .BUS_3(BUS_3[1]));
  ALU_bit _5 (
    .in_6(in_9), .in_7(in_4), .in_8(in_6), .in_9(in_10), .in_10(in_11), .in_11(in_3), .in_12(in_8),
    .in_13(in_5), .in_14(in_7), .bus_i(BUS_1[6]), .Bus_1___i(BUS_1[4]), .Bus_i__1(BUS_1[5]),
    .bus_2i(BUS_2[5]), .in_1(COUT4), .CARRY_OUT(COUT5), .BUS_3(BUS_3[5]));
  ALU_bit _9 (
    .in_6(in_9), .in_7(in_4), .in_8(in_6), .in_9(in_10), .in_10(in_11), .in_11(in_3), .in_12(in_8),
    .in_13(in_5), .in_14(in_7), .bus_i(BUS_1[10]), .Bus_1___i(BUS_1[8]), .Bus_i__1(BUS_1[9]),
    .bus_2i(BUS_2[9]), .in_1(COUT8), .CARRY_OUT(COUT9), .BUS_3(BUS_3[9]));
  ALU_bit _13 (
    .in_6(in_9), .in_7(in_4), .in_8(in_6), .in_9(in_10), .in_10(in_11), .in_11(in_3), .in_12(in_8),
    .in_13(in_5), .in_14(in_7), .bus_i(BUS_1[14]), .Bus_1___i(BUS_1[12]), .Bus_i__1(BUS_1[13]),
    .bus_2i(BUS_2[13]), .in_1(COUT12), .CARRY_OUT(COUT13), .BUS_3(BUS_3[13]));
  ALU_bit _2 (
    .in_6(in_9), .in_7(in_4), .in_8(in_6), .in_9(in_10), .in_10(in_11), .in_11(in_3), .in_12(in_8),
    .in_13(in_5), .in_14(in_7), .bus_i(BUS_1[3]), .Bus_1___i(BUS_1[1]), .Bus_i__1(BUS_1[2]),
    .bus_2i(BUS_2[2]), .in_1(COUT1), .CARRY_OUT(COUT2), .BUS_3(BUS_3[2]));
  ALU_bit _6 (
    .in_6(in_9), .in_7(in_4), .in_8(in_6), .in_9(in_10), .in_10(in_11), .in_11(in_3), .in_12(in_8),
    .in_13(in_5), .in_14(in_7), .bus_i(BUS_1[7]), .Bus_1___i(BUS_1[5]), .Bus_i__1(BUS_1[6]),
    .bus_2i(BUS_2[6]), .in_1(COUT5), .CARRY_OUT(COUT6), .BUS_3(BUS_3[6]));
  ALU_bit _10 (
    .in_6(in_9), .in_7(in_4), .in_8(in_6), .in_9(in_10), .in_10(in_11), .in_11(in_3), .in_12(in_8),
    .in_13(in_5), .in_14(in_7), .bus_i(BUS_1[11]), .Bus_1___i(BUS_1[9]), .Bus_i__1(BUS_1[10]),
    .bus_2i(BUS_2[10]), .in_1(COUT9), .CARRY_OUT(COUT10), .BUS_3(BUS_3[10]));
  ALU_bit _14 (
    .in_6(in_9), .in_7(in_4), .in_8(in_6), .in_9(in_10), .in_10(in_11), .in_11(in_3), .in_12(in_8),
    .in_13(in_5), .in_14(in_7), .bus_i(BUS_1[15]), .Bus_1___i(BUS_1[13]), .Bus_i__1(BUS_1[14]),
    .bus_2i(BUS_2[14]), .in_1(COUT13), .CARRY_OUT(COUT14), .BUS_3(BUS_3[14]));
  ALU_bit _3 (
    .in_6(in_9), .in_7(in_4), .in_8(in_6), .in_9(in_10), .in_10(in_11), .in_11(in_3), .in_12(in_8),
    .in_13(in_5), .in_14(in_7), .bus_i(BUS_1[4]), .Bus_1___i(BUS_1[2]), .Bus_i__1(BUS_1[3]),
    .bus_2i(BUS_2[3]), .in_1(COUT2), .CARRY_OUT(COUT3), .BUS_3(BUS_3[3]));
  ALU_bit _7 (
    .in_6(in_9), .in_7(in_4), .in_8(in_6), .in_9(in_10), .in_10(in_11), .in_11(in_3), .in_12(in_8),
    .in_13(in_5), .in_14(in_7), .bus_i(BUS_1[8]), .Bus_1___i(BUS_1[6]), .Bus_i__1(BUS_1[7]),
    .bus_2i(BUS_2[7]), .in_1(COUT6), .CARRY_OUT(COUT7), .BUS_3(BUS_3[7]));
  ALU_bit _11 (
    .in_6(in_9), .in_7(in_4), .in_8(in_6), .in_9(in_10), .in_10(in_11), .in_11(in_3), .in_12(in_8),
    .in_13(in_5), .in_14(in_7), .bus_i(BUS_1[12]), .Bus_1___i(BUS_1[10]), .Bus_i__1(BUS_1[11]),
    .bus_2i(BUS_2[11]), .in_1(COUT10), .CARRY_OUT(COUT11), .BUS_3(BUS_3[11]));
  ALU_bit _15 (
    .in_6(in_9), .in_7(in_4), .in_8(in_6), .in_9(in_10), .in_10(in_11), .in_11(in_3), .in_12(in_8),
    .in_13(in_5), .in_14(in_7), .bus_i(BUS_1[15]), .Bus_1___i(BUS_1[14]), .Bus_i__1(BUS_1[15]),
    .bus_2i(BUS_2[15]), .in_1(COUT14), .CARRY_OUT(out_14), .BUS_3(BUS_3[15]));
  and and_1 (out_13, ~BUS_3[0], ~BUS_3[1], ~BUS_3[2], ~BUS_3[3], ~BUS_3[4], ~BUS_3[5], ~BUS_3[6], ~BUS_3[7], ~BUS_3[8], ~BUS_3[9], ~BUS_3[10], ~BUS_3[11], ~BUS_3[12], ~BUS_3[13], ~BUS_3[14], ~BUS_3[15]);  // AND_Gate

  // Other names for the same wires on the sheet: ADD = in_9; AND = in_6; BUS10 = BUS_1[0]; BUS11 = BUS_1[1];
  //   BUS12 = BUS_1[2]; BUS13 = BUS_1[3]; BUS14 = BUS_1[4]; BUS15 = BUS_1[5]; BUS16 = BUS_1[6]; BUS17 = BUS_1[7];
  //   BUS18 = BUS_1[8]; BUS19 = BUS_1[9]; BUS110 = BUS_1[10]; BUS111 = BUS_1[11]; BUS112 = BUS_1[12];
  //   BUS113 = BUS_1[13]; BUS114 = BUS_1[14]; BUS115 = BUS_1[15]; BUS20 = BUS_2[0]; BUS21 = BUS_2[1];
  //   BUS22 = BUS_2[2]; BUS23 = BUS_2[3]; BUS24 = BUS_2[4]; BUS25 = BUS_2[5]; BUS26 = BUS_2[6]; BUS27 = BUS_2[7];
  //   BUS28 = BUS_2[8]; BUS29 = BUS_2[9]; BUS210 = BUS_2[10]; BUS211 = BUS_2[11]; BUS212 = BUS_2[12];
  //   BUS213 = BUS_2[13]; BUS214 = BUS_2[14]; BUS215 = BUS_2[15]; BUS30 = BUS_3[0]; BUS31 = BUS_3[1];
  //   BUS32 = BUS_3[2]; BUS33 = BUS_3[3]; BUS34 = BUS_3[4]; BUS35 = BUS_3[5]; BUS36 = BUS_3[6]; BUS37 = BUS_3[7];
  //   BUS38 = BUS_3[8]; BUS39 = BUS_3[9]; BUS310 = BUS_3[10]; BUS311 = BUS_3[11]; BUS312 = BUS_3[12];
  //   BUS313 = BUS_3[13]; BUS314 = BUS_3[14]; BUS315 = BUS_3[15]; NOT = in_11; OR = in_10; SHL = in_8; SHR = in_5;
  //   SUB = in_4; TCP = in_3; TRA1 = in_7

  // Notes on the sheet:
  //   1
  //   1
  //   1
  //   1
  //   1
  //   1
  //   1
  //   1
  //   1
  //   1
  //   1
  //   1
  //   1
  //   1
  //   1
  //   1
endmodule

module main (
  input  [15:0] in_1,
  input  [15:0] in_2,
  input  CLRMEM,
  input  DATA,
  input  START,
  input  in_6
);

  wire _1toB2, ADD, AND, and_1_out, and_14_out, and_15_out, and_16_out, and_17_out, and_18_out, and_19_out,
       and_20_out, and_21_out, B3toGPR2, B3toGPRD, B3toGPRT, B3toIR, B3toMAR, B3toMBR, B3toPC, B3toR0,
       B3toR1, B3toR2, B3toR3, bMicro, button_1_out, CC0, CC1, CC2, CC3, CC4, CC5, CC6, CLK, DATA_t, ERROR,
       GPRStoB1, GPRStoB2, GPRTtoB1, GPRTtoB2, INPUT, IR0P, IR1P, IR2P, IR3P, IR4P, IR5P, MBRtoB1, MEMtoMBR,
       mS0, mS1, n8reg44_1_p3, NOT, not_2_out, OR, or_1_out, OUTPUT, PCtoB1, R0toB1, R0toB2, R1toB1, R1toB2,
       R2toB1, R2toB2, R3toB1, R3toB2, RD0toB1, RD0toB2, RD1toB1, RD1toB2, RD2toB1, RD2toB2, RD3toB1,
       RD3toB2, register_1_p5, register_1_p6, register_4_p1, RS0toB1, RS0toB2, RS1toB1, RS1toB2, RS2toB1,
       RS2toB2, RS3toB1, RS3toB2, RT0toB1, RT0toB2, RT1toB1, RT1toB2, RT2toB1, RT2toB2, RT3toB1, RT3toB2,
       SHL, SHR, SIGN, SIMMtoB2, START_t, SUB, TARGETtoB1, TCP, TRA1, tri_state_buffer_9_p2,
       tri_state_buffer_11_p2, tri_state_buffer_13_p2, tri_state_buffer_15_p2, UPIMMtoB1, USIMMtoB2, WRITE,
       ZERO;
  wire [0:0] register_7_q;
  wire [3:0] _8to11, PC;
  wire [7:0] adder_1_out, adder_2_out, MicroAddress, multiplexer_3_out, n8reg44_1_p4;
  wire [11:0] register_3_p4;
  wire [14:0] register_1_p1;
  wire [15:0] IR, MemOUT, multiplexer_1_out, multiplexer_2_out, register_1_p4, rom_1_data,
       tri_state_buffer_1_p3, tri_state_buffer_3_p1, tri_state_buffer_7_p2;
  wire [31:0] rom_2_data;

  // Probe on {SIGN, register_1_p1}
  Multiplexer #(.width(16), .enable("false")) multiplexer_1 (
    .in0({SIGN, register_1_p1}), .in1(MemOUT), .out(multiplexer_1_out), .sel(MEMtoMBR));
  Multiplexer #(.width(16)) multiplexer_2 (
    .in0({SIGN, register_1_p1}), .in1(in_1), .out(multiplexer_2_out), .sel(button_1_out));  // open: en
  Button button_1 (.out(button_1_out));
  // Register register_1: pin names not known; wires that end beside it: {SIGN, register_1_p1}, in_6, B3toMAR, register_1_p4, register_1_p5, register_1_p6
  // Probe on multiplexer_1_out
  and and_1 (and_1_out, B3toPC, ~button_1_out);  // AND_Gate
  // Probe on register_1_p4
  // Register register_2: pin names not known; wires that end beside it: multiplexer_1_out, in_6, B3toMBR, register_1_p5
  // Probe on {PC, register_3_p4}
  // Register register_3: pin names not known; wires that end beside it: multiplexer_2_out, in_6, and_1_out, {PC, register_3_p4}
  not not_1 (register_1_p6, WRITE);
  // Probe on register_1_p5
  // Tri_State_Buffer tri_state_buffer_1: pin names not known; wires that end beside it: PCtoB1, {PC, register_3_p4}, tri_state_buffer_1_p3
  // Probe on MemOUT
  RAM #(.addrWidth(16), .dataWidth(16)) ram_1 (
    .addr(register_1_p4), .data(MemOUT), .sel(1'b1), .clk(register_1_p6), .ld(WRITE), .clr(CLRMEM));
  // Tri_State_Buffer tri_state_buffer_2: pin names not known; wires that end beside it: MBRtoB1, register_1_p5, tri_state_buffer_1_p3
  not not_2 (not_2_out, INPUT);
  // Tri_State_Buffer tri_state_buffer_3: pin names not known; wires that end beside it: tri_state_buffer_3_p1, 16'h1, _1toB2
  // Tri_State_Buffer tri_state_buffer_4: pin names not known; wires that end beside it: tri_state_buffer_1_p3, {PC, _8to11, IR[7:0]}, TARGETtoB1
  // Probe on tri_state_buffer_1_p3
  // Tri_State_Buffer tri_state_buffer_5: pin names not known; wires that end beside it: not_2_out, in_2, tri_state_buffer_1_p3
  // Tri_State_Buffer tri_state_buffer_6: pin names not known; wires that end beside it: tri_state_buffer_3_p1, {{8{1'b0}}, IR[7:0]}, USIMMtoB2
  // Probe on tri_state_buffer_3_p1
  // Tri_State_Buffer tri_state_buffer_7: pin names not known; wires that end beside it: tri_state_buffer_3_p1, tri_state_buffer_7_p2, SIMMtoB2
  // Tri_State_Buffer tri_state_buffer_8: pin names not known; wires that end beside it: tri_state_buffer_1_p3, {IR[7:0], {8{1'b0}}}, UPIMMtoB1, IR[7:0]
  assign tri_state_buffer_7_p2 = {{8{IR[7]}}, IR[7:0]};  // Bit_Extender bit_extender_1
  // Tri_State_Buffer tri_state_buffer_9: pin names not known; wires that end beside it: tri_state_buffer_3_p1, tri_state_buffer_9_p2, R1toB2
  // Tri_State_Buffer tri_state_buffer_10: pin names not known; wires that end beside it: tri_state_buffer_1_p3, tri_state_buffer_9_p2, R1toB1
  // Tri_State_Buffer tri_state_buffer_11: pin names not known; wires that end beside it: tri_state_buffer_3_p1, tri_state_buffer_11_p2, R3toB2
  // Tri_State_Buffer tri_state_buffer_12: pin names not known; wires that end beside it: tri_state_buffer_1_p3, tri_state_buffer_11_p2, R3toB1
  // Probe on {SIGN, register_1_p1}
  ALU_16 alu_16_1 (
    .in_3(TCP), .in_4(SUB), .in_5(SHR), .in_6(AND), .in_7(TRA1), .in_8(SHL), .in_9(ADD), .in_10(OR),
    .in_11(NOT), .out_13(ZERO), .BUS_1(tri_state_buffer_1_p3), .BUS_2(tri_state_buffer_3_p1),
    .BUS_3({SIGN, register_1_p1}));  // open: out_14
  // Register GPR1: pin names not known; wires that end beside it: tri_state_buffer_9_p2, B3toR1, in_6, {SIGN, register_1_p1}
  // Tri_State_Buffer tri_state_buffer_13: pin names not known; wires that end beside it: tri_state_buffer_3_p1, tri_state_buffer_13_p2, R2toB2
  // Tri_State_Buffer tri_state_buffer_14: pin names not known; wires that end beside it: tri_state_buffer_1_p3, tri_state_buffer_13_p2, R2toB1
  // Register GPR3: pin names not known; wires that end beside it: tri_state_buffer_11_p2, B3toR3, in_6, {SIGN, register_1_p1}
  // Probe on register_4_p1
  // Register register_4: pin names not known; wires that end beside it: register_4_p1, OUTPUT, in_6, {SIGN, register_1_p1}, {SIGN, register_1_p1}
  // Probe on {IR[15:12], _8to11, IR[7:0]}
  // Tri_State_Buffer tri_state_buffer_15: pin names not known; wires that end beside it: tri_state_buffer_3_p1, tri_state_buffer_15_p2, R0toB2
  // Tri_State_Buffer tri_state_buffer_16: pin names not known; wires that end beside it: tri_state_buffer_1_p3, tri_state_buffer_15_p2, R0toB1
  // Register register_5: pin names not known; wires that end beside it: {IR[12], IR[5:0]}, {IR[15:12], _8to11, IR[7:0]}, B3toIR, in_6, {SIGN, register_1_p1}
  // Probe on tri_state_buffer_15_p2
  // Register GPR0: pin names not known; wires that end beside it: tri_state_buffer_15_p2, B3toR0, in_6, {SIGN, register_1_p1}
  // Probe on tri_state_buffer_13_p2
  // Register GPR2: pin names not known; wires that end beside it: tri_state_buffer_13_p2, B3toR2, in_6, {SIGN, register_1_p1}
  and and_2 (B3toR3, RD3toB2, RD3toB1);
  and and_3 (B3toR2, RD2toB2, B3toGPR2, RD2toB1);
  and and_4 (B3toR1, RD1toB2, RD1toB1);
  and and_5 (B3toR0, RD0toB2, RD0toB1);
  and and_6 (R3toB2, RT3toB2, RS3toB2);
  and and_7 (R2toB2, RT2toB2, RS2toB2);
  and and_8 (R1toB2, RT1toB2, RS1toB2);
  and and_9 (R0toB2, RT0toB2, RS0toB2);
  and and_10 (R3toB1, RT3toB1, RS3toB1);
  and and_11 (R2toB1, RT2toB1, RS2toB1);
  and and_12 (R1toB1, RT1toB1, RS1toB1);
  and and_13 (R0toB1, RT0toB1, RS0toB1);
  // _2x4Dec 2x4dec_1: pin names not known; wires that end beside it: RD3toB2, RD2toB2, RD1toB2, RD0toB2, _8to11[1:0], B3toGPRT
  // _2x4Dec 2x4dec_2: pin names not known; wires that end beside it: RD3toB1, RD2toB1, RD1toB1, RD0toB1, IR[7:6], B3toGPRD
  // _2x4Dec 2x4dec_3: pin names not known; wires that end beside it: RT3toB2, RT2toB2, RT1toB2, RT0toB2, _8to11[1:0], GPRTtoB2
  // _2x4Dec 2x4dec_4: pin names not known; wires that end beside it: RS3toB2, RS2toB2, RS1toB2, RS0toB2, _8to11[3:2], GPRStoB2
  // _2x4Dec 2x4dec_5: pin names not known; wires that end beside it: RT3toB1, RT2toB1, RT1toB1, RT0toB1, _8to11[1:0], GPRTtoB1
  // _2x4Dec 2x4dec_6: pin names not known; wires that end beside it: RS3toB1, RS2toB1, RS1toB1, RS0toB1, _8to11[3:2], GPRStoB1
  Clock #(.highDuration(100), .lowDuration(100)) clock_1 (.out(CLK));
  Control_Unit control_unit_1 (.out_4(DATA_t), .B(DATA), .INPUT(CLK), .RESET(in_6));
  or or_1 (or_1_out, SIGN, ZERO);
  and and_14 (and_14_out, CC3, ~ZERO);  // AND_Gate
  and and_15 (and_15_out, CC4, ZERO);
  and and_16 (and_16_out, CC5, ~SIGN);  // AND_Gate
  and and_17 (and_17_out, CC6, or_1_out);
  and and_18 (and_18_out, ~START_t, bMicro);  // AND_Gate
  and and_19 (and_19_out, ~START_t, CC1);  // AND_Gate
  and and_20 (and_20_out, CC2, ~DATA_t);  // AND_Gate
  Control_Unit control_unit_2 (.out_4(START_t), .B(START), .INPUT(CLK), .RESET(in_6));
  Adder adder_1 (.a(n8reg44_1_p4), .b(8'h1), .out(adder_1_out), .cin(1'b0));  // open: cout
  or or_2 (mS1, START_t, CC1);
  or or_3 (mS0, and_18_out, and_19_out);
  or or_4 (bMicro, CC0, and_20_out, and_14_out, and_15_out, and_16_out, and_17_out);
  Multiplexer #(.select(2), .width(8), .enable("false")) multiplexer_3 (
    .in0(adder_1_out), .in1(MicroAddress), .in2(8'h50), .in3(adder_2_out), .out(multiplexer_3_out),
    .sel({mS1, mS0}));
  // _8Reg44 8reg44_1: pin names not known; wires that end beside it: multiplexer_3_out, in_6, n8reg44_1_p3, n8reg44_1_p4, {_8to11, IR[7:0]}
  not not_3 (n8reg44_1_p3, CLK);
  ROM #(.dataWidth(16)) rom_1 (.addr(n8reg44_1_p4), .data(rom_1_data), .sel(1'b1));
  Hex_Digit_Display hex_digit_display_1 (.value(n8reg44_1_p4[3:0]));  // open: dp
  Hex_Digit_Display hex_digit_display_2 (.value(n8reg44_1_p4[7:4]));  // open: dp
  Register #(.width(16)) register_6 (
    .D(rom_1_data), .en(1'b1), .Q({CC6, CC5, CC4, CC3, CC2, CC1, CC0, MicroAddress, ADD}), .clk(CLK),
    .clr(1'b0));
  Adder adder_2 (
    .a({4'b0000, IR[15:12]}), .b({2'b00, IR5P, IR4P, IR3P, IR2P, IR1P, IR0P}), .out(adder_2_out), .cin(1'b0));  // open: cout
  and and_21 (and_21_out, IR[12], IR[13], IR[14], IR[15]);
  ROM #(.dataWidth(32)) rom_2 (.addr(n8reg44_1_p4), .data(rom_2_data), .sel(1'b1));
  Register #(.width(32)) register_7 (
    .D(rom_2_data), .en(1'b1),
    .Q({SUB, AND, OR, NOT, TCP, SHL, SHR, TRA1, PCtoB1, MBRtoB1, GPRStoB1, GPRTtoB1, UPIMMtoB1, TARGETtoB1, GPRStoB2, GPRTtoB2, SIMMtoB2, USIMMtoB2, _1toB2, B3toPC, B3toIR, B3toMAR, B3toMBR, B3toGPRD, B3toGPRT, B3toGPR2, MEMtoMBR, WRITE, INPUT, OUTPUT, ERROR, register_7_q[0]}),
    .clk(CLK), .clr(1'b0));
  and and_22 (IR0P, IR[0], and_21_out);
  and and_23 (IR1P, IR[1], and_21_out);
  and and_24 (IR2P, IR[2], and_21_out);
  and and_25 (IR3P, IR[3], and_21_out);
  and and_26 (IR4P, IR[4], and_21_out);
  and and_27 (IR5P, IR[5], and_21_out);

  // Other names for the same wires on the sheet: IR12_15[3:0] = IR[15:12]; RD[1:0] = IR[7:6]; IR[11:8] = _8to11;
  //   RT[1:0] = _8to11[1:0]; RS[1:0] = _8to11[3:2]; CLR = in_6; RESET = in_6

  // Notes on the sheet:
  //   there was a button here going to a RESET tunnel. may he rest in peace
  //   PC
  //   IR
  //   THESE BOXES ARE PROBABLY OUT OF ORDER..... LOL
  //   put the q part of the IR on the IR tunnel. delete the 0000 bus thingy
  //   one control unit. 2 buttons on the unit. for start and data
  //   Sadie
  //   Tiff
  //   micro MAR
  //   ROM
  //   IR0-11
  //   contents of rom_1 (hex, n*v repeats v):
  //   2ee 2f4 2fa 300 2c8 2cc 2d0 2e0 2e8 306 30a 4*29e 2a8 2ac 2b0 2b4 2b8 2bc 2c0 2c4 17*29e 310 314 2d4
  //   2da 258 31a 31c 33*29e 0 1 0 400 1 2a1 0 2a0 0 2a0 0 2a0 0 2a0 0 2a0 0 2a0 0 2a0 1 2a1 0 2a0 0 2a0
  //   8d4 0 2a0 0 8dc 2a0 1 0 0 2a0 1 0 2a0 20a0 1 2a0 10a0 1 2a0 80a0 1 2a0 40a0 1 2a0 0 2a0 0 0 2a0 0
  //   2a0 0 0 2a0 2a0 2a0
  //   register
  //   Kevin
  //   ROM
  //   contents of rom_2 (hex, n*v repeats v):
  //   79*ffffd0 ffffd2 17ffbd0 7fcdf0 1bff7d0 ffffd0 defed0 deffd0 80defed0 80deffd0 40defed0 40deffd0
  //   20defed0 20deffd0 10fdfed0 10fdffd0 8fdfed0 8fdffd0 4dffed0 4dfffd0 2dffed0 2dfffd0 df7f50 df7fd0
  //   20dfbf50 20dfbfd0 1f7ff50 1f7ffd0 ffffd8 1fffed8 1ffffd8 1dfffd0 1dfffd4 ffffd0 df7bf0 fffdf0
  //   1bfff50 1bfffd0 df7bd0 1effdd0 ffffc0 80deffd0 7f6fd0 ffffd0 80deffd0 7f6fd0 ffffd0 1dfffd0 7f6fd0
  //   ffffd0 1dfffd0 7f6fd0 ffffd0 1fbefd0 ffffd0 17fff90 1fbefd0 ffffd0 1dfefd0 ffffd0 17fff90 1dfefd0
  //   ffffd0 ffffd0 ffffd0
  //   register
endmodule

module AC (
  input  in_1,
  input  B,
  input  INPUT,
  output out_4
);

  wire and_1_out, and_2_out, Q0, Q0N, Q1, Q1N;

  and and_1 (and_1_out, Q0, ~B);  // AND_Gate
  and and_2 (and_2_out, Q1N, B);
  D_Flip_Flop D0 (.clk(INPUT), .D(and_1_out), .Q(Q0), .Qn(Q0N), .preset(1'b0), .en(1'b1), .reset(in_1));
  D_Flip_Flop D0_2 (.clk(INPUT), .D(and_2_out), .Q(Q1), .Qn(Q1N), .preset(1'b0), .en(1'b1), .reset(in_1));
  and and_3 (out_4, Q1, Q0N);

  // Other names for the same wires on the sheet: RESET = in_1
endmodule

module Control_Unit (
  input  RESET,
  input  B,
  input  INPUT,
  output out_4
);

  wire and_1_out, and_2_out, Q0, Q0N, Q1, Q1N, RESET_t;

  and and_1 (and_1_out, Q1, ~B);  // AND_Gate
  and and_2 (and_2_out, Q0N, B);
  D_Flip_Flop D0 (.clk(INPUT), .D(and_1_out), .Q(Q0), .Qn(Q0N), .preset(1'b0), .en(1'b1), .reset(RESET_t));
  D_Flip_Flop D1 (.clk(INPUT), .D(and_2_out), .Q(Q1), .Qn(Q1N), .preset(1'b0), .en(1'b1), .reset(RESET_t));
  not not_1 (RESET_t, RESET);
  and and_3 (out_4, Q1, Q0N);
endmodule
